# Fritzing sketch Sketch (saved by Fritzing 0.9.3b)
breadboards: 1

parts:
  Part2 = Arduino Uno (Rev3) - ICSP
  J1 = Piezo Speaker
  Load_Cell1 = Load Cell - Red/white/black/green
  PART1 = SparkFun Load Cell Amplifier - HX711 [part_number=SEN-13230]

nets:
  N1: Part2.D5_PWM, PART1.CLK
  N2: Part2.D6_PWM, PART1.DAT
  N3: Part2.D7, J1.pin2
  5V: Part2.5V, PART1.VCC
  GND: Part2.GND, PART1.GND
  N4: Load_Cell1.wire1, PART1.RED
  N5: Load_Cell1.wire2, PART1.WHT
  N6: Load_Cell1.wire3, PART1.BLK
  N7: Load_Cell1.wire4, PART1.GRN

custom parts:
  Load Cell - Red/white/black/green: A rectangle load cell/weighting pressure Sensor with four wires - Red, white, black, green. Normally corresponding with E+, E-, A+, A- respectively.
  SparkFun Load Cell Amplifier - HX711: The SparkFun Load Cell Amplifier is a small breakout board for the HX711 IC that allows you to easily read load cells to measure weight. By connecting the amplifier to your microcontroller you will be able to read the changes in the resistance of the load cell and with some calibration you’ll be able to get very accurate weight measurements. This can be handy for creating your own industrial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
