# Fritzing sketch Sketch2.0 (saved by Fritzing 0.9.3b)
breadboards: 1

parts:
  Part2 = Arduino Uno (Rev3) - ICSP
  J1 = Piezo Speaker
  J2 = Basic Force Sensing Resistor (FSR) [package=THT]
  R1 = Resistor [tolerance=±5% resistance=220 package="2010 [SMD]"]  # not connected
  R2 = Resistor [tolerance=±5% resistance=220 package=THT]

nets:
  N1: Part2.A0, J2.pin_1
  N2: Part2.GND, J1.pin1, J2.pin_0
  N3: J1.pin2, R2.Pin_0
